// Digital circuit project07ExtraCredit.dig as structural Verilog
module project07ExtraCredit (
  input  [4:0] PROG,
  input  CLK,
  input  CLR,
  input  EN,
  output [63:0] A0,
  output [63:0] A1,
  output [63:0] A2,
  output DONE,
  output [63:0] zero,
  output [63:0] ra,
  output [63:0] sp,
  output [63:0] gp,
  output [63:0] tp,
  output [63:0] t0,
  output [63:0] t1,
  output [63:0] t2,
  output [63:0] s0_fp,
  output [63:0] s1,
  output [63:0] a0_2,
  output [63:0] a1_2,
  output [63:0] a2_2,
  output [63:0] a3,
  output [63:0] a4,
  output [63:0] a5,
  output [63:0] a6,
  output [63:0] a7,
  output [63:0] s2,
  output [63:0] s3,
  output [63:0] s4,
  output [63:0] s5,
  output [63:0] s6,
  output [63:0] s7,
  output [63:0] s8,
  output [63:0] s9,
  output [63:0] s10,
  output [63:0] s11,
  output [63:0] t3,
  output [63:0] t4,
  output [63:0] t5,
  output [63:0] t6,
  output [63:0] A3_2
);

  wire _01_dr_ex_register_1_p27, _02_ex_mem_register_1_p21, ALOp_1, ALOp_2, ALUA_1, ALUA_2, ALUB_1,
       and_2_out, BUOp_1, BUOp_2, CLK_t, DREX_CLR, DREX_EN, EXMEM_CLR, IFDR_CLR, inst_memextracredit_1_p8,
       inst_memextracredit_1_p9, iw_0, iw_1, iw_2, iw_3, iw_to_ascii_1_p2, iw_to_ascii_1_p3,
       iw_to_ascii_1_p4, iw_to_ascii_1_p5, iw_to_ascii_2_p2, iw_to_ascii_2_p3, iw_to_ascii_2_p4,
       iw_to_ascii_2_p5, iw_to_ascii_3_p2, iw_to_ascii_3_p3, iw_to_ascii_3_p4, iw_to_ascii_3_p5,
       iw_to_ascii_4_p7, iw_to_ascii_4_p8, iw_to_ascii_4_p9, iw_to_ascii_4_p10, iw_to_ascii_5_p5,
       iw_to_ascii_5_p6, iw_to_ascii_5_p7, iw_to_ascii_5_p8, MLD_1, MLD_2, MLD_3, MR_1, MR_2, MR_3, MR_4,
       MST_1, MST_2, MST_3, MSZ_1, MSZ_2, MSZ_3, not_1_out, PCbr_2, PCbr_3, PCbr_4, PCsl_1, PCsl_2,
       register_file_1_p8, register_file_1_p9, RFW_1, RFW_2, RFW_3, RFW_4, RR0_1, RR0_3, RR0_4, RR1_1, RR1_3,
       RR1_4, WDsl_1, WDsl_2, WDsl_3, WDsl_4, WR_1, WR_2;
  wire [1:0] FRD_0, FRD_1;
  wire [2:0] ALUB_2;
  wire [4:0] RR0_2, RR1_2, WR_3, WR_4;
  wire [31:0] iw_4;
  wire [63:0] _01_dr_ex_register_1_p26, _02_ex_mem_register_1_p20, _03_mem_wb_register_1_p16,
       _03_mem_wb_register_1_p17, _03_mem_wb_register_1_p18, ALUR_3, decoder_imm_1_p2, decoder_imm_1_p3,
       decoder_imm_1_p4, decoder_imm_1_p5, decoder_imm_1_p6, decoder_imm_1_p7, MR_OUT, multiplexer_1_out,
       multiplexer_2_out, multiplexer_3_out, multiplexer_4_out, multiplexer_5_out, multiplexer_6_out, PC,
       PC_plus_4_s, ramdualport_1_d, RD0_2, RD1_2, TA;

  Multiplexer #(.Bits(64)) multiplexer_1 (.sel(PCbr_2), .in_0(PC_plus_4_s), .in_1(TA), .out(multiplexer_1_out));
  // register_with_clr_64bits PC: pin names not known; wires that end beside it: multiplexer_1_out, CLK_t, DREX_EN, CLR, PC
  and and_1 (CLK_t, CLK, ~DONE);  // And
  Comparator #(.Bits(32)) End (.a(iw_4), .b(32'hc0001073), .eq(DONE));  // open: gt, lt
  LED led_1 (.in(DONE));
  Add #(.Bits(64)) PC_plus_4 (.a(PC), .b(64'h4), .c_i(1'b0), .s(PC_plus_4_s));  // open: c_o
  // Probe on iw_to_ascii_1_p2
  // iw_to_ascii iw_to_ascii_1: pin names not known; wires that end beside it: iw_0, iw_to_ascii_1_p2, iw_to_ascii_1_p3, iw_to_ascii_1_p4, iw_to_ascii_1_p5
  // inst_memExtraCredit inst_memextracredit_1: pin names not known; wires that end beside it: PROG, PC[10:2], iw_0, PC, PC_plus_4_s, CLK_t, DREX_EN, inst_memextracredit_1_p8, inst_memextracredit_1_p9
  // Probe on iw_to_ascii_1_p4
  // Probe on iw_to_ascii_1_p3
  // Probe on iw_to_ascii_1_p5
  // _00_IF_DR_register _00_if_dr_register_1: pin names not known; wires that end beside it: iw_0, iw_1
  // decoder_inst decoder_inst_1: pin names not known; wires that end beside it: iw_1, MSZ_1, MST_1, MLD_1, MR_1, BUOp_1, WDsl_1, PCsl_1, ALUB_1, ALUA_1, ALOp_1, RFW_1
  // decoder_reg decoder_reg_1: pin names not known; wires that end beside it: iw_1, RR0_1, RR1_1, WR_1
  Multiplexer #(.Bits(64)) multiplexer_2 (
    .sel(WDsl_4), .in_0(MR_OUT), .in_1(_03_mem_wb_register_1_p18), .out(multiplexer_2_out));
  and and_2 (and_2_out, RFW_4, EN);
  not not_1 (not_1_out, CLK_t);
  // Probe on iw_to_ascii_2_p2
  // iw_to_ascii iw_to_ascii_2: pin names not known; wires that end beside it: iw_1, iw_to_ascii_2_p2, iw_to_ascii_2_p3, iw_to_ascii_2_p4, iw_to_ascii_2_p5
  // register_file register_file_1: pin names not known; wires that end beside it: RR0_1, RR1_1, WR_4, and_2_out, multiplexer_2_out, not_1_out, CLR, register_file_1_p8, register_file_1_p9, zero, ra, sp, gp, tp, t0, t1, t2, s0_fp, s1, A0, A1, A2, a3, a4, a5, a6, a7, s2, s3, s4, s5, s6
  // Probe on iw_to_ascii_2_p4
  // Probe on iw_to_ascii_2_p3
  // Probe on iw_to_ascii_2_p5
  // _01_DR_EX_register _01_dr_ex_register_1: pin names not known; wires that end beside it: iw_1, RR0_1, RR1_1, WR_1, register_file_1_p8, register_file_1_p9, inst_memextracredit_1_p8, inst_memextracredit_1_p9, MSZ_1, MST_1, MLD_1, MR_1, BUOp_1, WDsl_1, PCsl_1, ALUB_1, ALUA_1, ALOp_1, RFW_1, iw_2, RR0_2, RR1_2, WR_2, RD0_2, RD1_2, _01_dr_ex_register_1_p26, _01_dr_ex_register_1_p27, MSZ_2, MST_2, MLD_2, MR_2, BUOp_2, WDsl_2, PCsl_2, ALUB_2, ALUA_2, ALOp_2
  Multiplexer #(.Selector_Bits(2), .Bits(64)) multiplexer_3 (
    .sel(FRD_0), .in_0(RD0_2), .in_1(ALUR_3), .in_2(MR_OUT), .in_3({64{1'b0}}), .out(multiplexer_3_out));
  Multiplexer #(.Selector_Bits(2), .Bits(64)) multiplexer_4 (
    .sel(FRD_1), .in_0(RD1_2), .in_1(ALUR_3), .in_2(MR_OUT), .in_3({64{1'b0}}), .out(multiplexer_4_out));
  // Probe on iw_to_ascii_3_p2
  // iw_to_ascii iw_to_ascii_3: pin names not known; wires that end beside it: iw_2, iw_to_ascii_3_p2, iw_to_ascii_3_p3, iw_to_ascii_3_p4, iw_to_ascii_3_p5
  // decoder_imm decoder_imm_1: pin names not known; wires that end beside it: iw_2, decoder_imm_1_p2, decoder_imm_1_p3, decoder_imm_1_p4, decoder_imm_1_p5, decoder_imm_1_p6, decoder_imm_1_p7
  // Probe on iw_to_ascii_3_p4
  // Probe on iw_to_ascii_3_p3
  // Probe on iw_to_ascii_3_p5
  // branch_unit branch_unit_1: pin names not known; wires that end beside it: multiplexer_3_out, multiplexer_4_out, PCsl_2, BUOp_2, PCbr_2
  Multiplexer #(.Bits(64)) multiplexer_5 (
    .sel(ALUA_2), .in_0(multiplexer_3_out), .in_1(_01_dr_ex_register_1_p26), .out(multiplexer_5_out));
  Multiplexer #(.Selector_Bits(3), .Bits(64)) multiplexer_6 (
    .sel(ALUB_2), .in_0(multiplexer_4_out), .in_1(decoder_imm_1_p2), .in_2(decoder_imm_1_p6),
    .in_3(decoder_imm_1_p5), .in_4(decoder_imm_1_p4), .in_5(decoder_imm_1_p7), .in_6(decoder_imm_1_p3),
    .in_7({64{1'b0}}), .out(multiplexer_6_out));
  // alu alu_1: pin names not known; wires that end beside it: multiplexer_5_out, multiplexer_6_out, ALOp_2, TA
  // _02_EX_MEM_register _02_ex_mem_register_1: pin names not known; wires that end beside it: iw_2, RR0_2, RR1_2, WR_2, TA, multiplexer_4_out, _01_dr_ex_register_1_p27, MSZ_2, MST_2, MLD_2, MR_2, WDsl_2, PCbr_2, RFW_2, iw_3, RR0_3, RR1_3, WR_3, ALUR_3, _02_ex_mem_register_1_p20, _02_ex_mem_register_1_p21, MSZ_3, MST_3, MLD_3, MR_3
  // Probe on iw_to_ascii_4_p7
  // iw_to_ascii iw_to_ascii_4: pin names not known; wires that end beside it: CLK_t, 1'b1, EXMEM_CLR, PCbr_3, RFW_3, iw_3, iw_to_ascii_4_p7, iw_to_ascii_4_p8, iw_to_ascii_4_p9, iw_to_ascii_4_p10
  // Probe on iw_to_ascii_4_p9
  // Probe on iw_to_ascii_4_p8
  HazardUnit hazardunit_1 (
    .RR0_2(RR0_2), .RR1_2(RR1_2), .WR_3(WR_3), .RFW_3(RFW_3), .WR_4(WR_4), .RFW_4(RFW_4), .MR_3(MR_3),
    .CLR(CLR), .PCbr_2(PCbr_2), .FRD_0(FRD_0), .FRD_1(FRD_1), .DREX_EN(DREX_EN), .EXMEM_CLR(EXMEM_CLR),
    .IFDR_CLR(IFDR_CLR), .DREX_CLR(DREX_CLR));
  // Probe on iw_to_ascii_4_p10
  RAMDualPort #(.AddrBits(7), .Bits(64)) ramdualport_1 (
    .A(ALUR_3[9:3]), .Din(_02_ex_mem_register_1_p20), .str(MST_3), .C(CLK_t), .ld(MLD_3), .D(ramdualport_1_d));
  // _03_MEM_WB_register _03_mem_wb_register_1: pin names not known; wires that end beside it: iw_3, RR0_3, RR1_3, WR_3, ALUR_3, ramdualport_1_d, _02_ex_mem_register_1_p21, MR_3, WDsl_3, PCbr_3, RFW_3, iw_4, RR0_4, RR1_4, WR_4, _03_mem_wb_register_1_p16, _03_mem_wb_register_1_p17, _03_mem_wb_register_1_p18, MR_4, WDsl_4, PCbr_4
  // Probe on iw_to_ascii_5_p5
  // iw_to_ascii iw_to_ascii_5: pin names not known; wires that end beside it: CLK_t, 1'b1, iw_4, CLR, iw_to_ascii_5_p5, iw_to_ascii_5_p6, iw_to_ascii_5_p7, iw_to_ascii_5_p8
  // Probe on iw_to_ascii_5_p7
  // Probe on iw_to_ascii_5_p6
  // Probe on iw_to_ascii_5_p8
  Multiplexer #(.Bits(64)) multiplexer_7 (
    .sel(MR_4), .in_0(_03_mem_wb_register_1_p16), .in_1(_03_mem_wb_register_1_p17), .out(MR_OUT));

  assign a0_2 = A0;
  assign a1_2 = A1;
  assign a2_2 = A2;
  assign A3_2 = a3;

  // Other names for the same wires on the sheet: x0[63:0] = zero; x1[63:0] = ra; x2[63:0] = sp; x3[63:0] = gp;
  //   x4[63:0] = tp; x5[63:0] = t0; x6[63:0] = t1; x7[63:0] = t2; x8[63:0] = s0_fp; x9[63:0] = s1; x10[63:0] = A0;
  //   x11[63:0] = A1; x12[63:0] = A2; x13[63:0] = a3; x14[63:0] = a4; x15[63:0] = a5; x16[63:0] = a6; x17[63:0] = a7;
  //   x18[63:0] = s2; x19[63:0] = s3; x20[63:0] = s4; x21[63:0] = s5; x22[63:0] = s6; x23[63:0] = s7; x24[63:0] = s8;
  //   x25[63:0] = s9; x26[63:0] = s10; x27[63:0] = s11; x28[63:0] = t3; x29[63:0] = t4; x30[63:0] = t6;
  //   x31[63:0] = t5

  // Notes on the sheet:
  //   CLK: Hz: 2147483647
  //   (0) IF Stage
  //   Instruction Fetch
  //   (1) DR Stage
  //   Decode Register Read
  //   (2) EX Stage
  //   Execute
  //   (3) MEM Stage
  //   Memory
  //   (4) WB Stage
  //   Write Back
endmodule

/* Test case 00-unit-add-i:
CLR EN CLK PROG A0 A1 A2 A3
1   0   0   x    x    x    x    x
0   0   0   x    x    x    x    x
while (!(DONE))
0   1   C   0    x    x    x    x
end while
0   1   0   0 3  0  0  0
*/

/* Test case 01-unit-add-r:
CLR EN CLK PROG A0 A1 A2 A3
1   0   0   x    x    x    x    x
0   0   0   x    x    x    x    x
while (!(DONE))
0   1   C   1    x    x    x    x
end while
0   1   0   1 9  6  0  0
*/

/* Test case 02-unit-jal:
CLR EN CLK PROG A0 A1 A2 A3
1   0   0   x    x    x    x    x
0   0   0   x    x    x    x    x
while (!(DONE))
0   1   C   2    x    x    x    x
end while
0   1   0   2 3  2  0  0
*/

/* Test case 03-unit-mul:
CLR EN CLK PROG A0 A1 A2 A3
1   0   0   x    x    x    x    x
0   0   0   x    x    x    x    x
while (!(DONE))
0   1   C   3    x    x    x    x
end while
0   1   0   3 21  7  0  0
*/

/* Test case 04-unit-sll-r:
CLR EN CLK PROG A0 A1 A2 A3
1   0   0   x    x    x    x    x
0   0   0   x    x    x    x    x
while (!(DONE))
0   1   C   4    x    x    x    x
end while
0   1   0   4 4  1  2  0
*/

/* Test case 05-unit-srl-r:
CLR EN CLK PROG A0 A1 A2 A3
1   0   0   x    x    x    x    x
0   0   0   x    x    x    x    x
while (!(DONE))
0   1   C   5    x    x    x    x
end while
0   1   0   5 4  8  1  0
*/

/* Test case 06-unit-slli:
CLR EN CLK PROG A0 A1 A2 A3
1   0   0   x    x    x    x    x
0   0   0   x    x    x    x    x
while (!(DONE))
0   1   C   6    x    x    x    x
end while
0   1   0   6 8  1  0  0
*/

/* Test case 07-unit-srli:
CLR EN CLK PROG A0 A1 A2 A3
1   0   0   x    x    x    x    x
0   0   0   x    x    x    x    x
while (!(DONE))
0   1   C   7    x    x    x    x
end while
0   1   0   7 8  32  0  0
*/

/* Test case 08-unit-j:
CLR EN CLK PROG A0 A1 A2 A3
1   0   0   x    x    x    x    x
0   0   0   x    x    x    x    x
while (!(DONE))
0   1   C   8    x    x    x    x
end while
0   1   0   8 1  0  0  0
*/

/* Test case 09-unit-beq:
CLR EN CLK PROG A0 A1 A2 A3
1   0   0   x    x    x    x    x
0   0   0   x    x    x    x    x
while (!(DONE))
0   1   C   9    x    x    x    x
end while
0   1   0   9 1  1  0  0
*/

/* Test case 10-unit-blt:
CLR EN CLK PROG A0 A1 A2 A3
1   0   0   x    x    x    x    x
0   0   0   x    x    x    x    x
while (!(DONE))
0   1   C   10    x    x    x    x
end while
0   1   0   10 1  2  0  0
*/

/* Test case 11-unit-bge:
CLR EN CLK PROG A0 A1 A2 A3
1   0   0   x    x    x    x    x
0   0   0   x    x    x    x    x
while (!(DONE))
0   1   C   11    x    x    x    x
end while
0   1   0   11 2  1  0  0
*/

/* Test case 12-unit-sd-ld:
CLR EN CLK PROG A0 A1 A2 A3
1   0   0   x    x    x    x    x
0   0   0   x    x    x    x    x
while (!(DONE))
0   1   C   12    x    x    x    x
end while
0   1   0   12 99  0  0  0
*/

/* Test case 13-unit-sw-lw:
CLR EN CLK PROG A0 A1 A2 A3
1   0   0   x    x    x    x    x
0   0   0   x    x    x    x    x
while (!(DONE))
0   1   C   13    x    x    x    x
end while
0   1   0   13 99  0  0  0
*/

/* Test case 14-unit-sb-lb:
CLR EN CLK PROG A0 A1 A2 A3
1   0   0   x    x    x    x    x
0   0   0   x    x    x    x    x
while (!(DONE))
0   1   C   14    x    x    x    x
end while
0   1   0   14 99  0  0  0
*/

/* Test case 15-prog-quadratic:
CLR EN CLK PROG A0 A1 A2 A3
1   0   0   x    x    x    x    x
0   0   0   x    x    x    x    x
while (!(DONE))
0   1   C   15    x    x    x    x
end while
0   1   0   15 25  3  4  5
*/

/* Test case 17-prog-fibrec:
CLR EN CLK PROG A0 A1 A2 A3
1   0   0   x    x    x    x    x
0   0   0   x    x    x    x    x
while (!(DONE))
0   1   C   17    x    x    x    x
end while
0   1   0   17 55  0  0  0
*/

/* Test case 18-prog-is-pal:
CLR EN CLK PROG A0 A1 A2 A3
1   0   0   x    x    x    x    x
0   0   0   x    x    x    x    x
while (!(DONE))
0   1   C   18    x    x    x    x
end while
0   1   0   18 1  3  3  0
*/

/* Test case 20-prog-swap:
CLR EN CLK PROG A0 A1 A2 A3
1   0   0   x    x    x    x    x
0   0   0   x    x    x    x    x
while (!(DONE))
0   1   C   20    x    x    x    x
end while
0   1   0   20 12  1  5  0
*/

/* Test case 16-prog-get-bitseq:
CLR EN CLK PROG A0 A1 A2 A3
1   0   0   x    x    x    x    x
0   0   0   x    x    x    x    x
while (!(DONE))
0   1   C   16    x    x    x    x
end while
0   1   0   16 6  12  15  0
*/

/* Test case 19-prog-to-upper:
CLR EN CLK PROG A0 A1 A2 A3
1   0   0   x    x    x    x    x
0   0   0   x    x    x    x    x
while (!(DONE))
0   1   C   19    x    x    x    x
end while
0   1   0   19 5066355251797426176  1014  0  0
*/

/* Test case 21-prog-sort:
CLR EN CLK PROG A0 A1 A2 A3
1   0   0   x    x    x    x    x
0   0   0   x    x    x    x    x
while (!(DONE))
0   1   C   21    x    x    x    x
end while
0   1   0   21 8589934596  25769803784  42949672972  0
*/
